// Logisim project solution-1.circ as structural Verilog: 4 circuits, main circuit s-1
module s_1 (
  input  in_1,
  input  in_2,
  input  in_3,
  output out_4
);

  wire and_1_out, and_2_out, not_1_out, not_2_out;

  not not_1 (not_1_out, in_2);
  not not_2 (not_2_out, in_3);
  and and_1 (and_1_out, in_1, not_1_out, not_2_out);
  and and_2 (and_2_out, in_2, in_3);
  or or_1 (out_4, and_1_out, and_2_out);
endmodule

module s_2 (
  input  in_1,
  input  in_2,
  output out_3
);

  wire nand_1_out, nand_2_out, nand_3_out, nand_4_out;

  nand nand_1 (nand_1_out, in_1, in_1);
  nand nand_2 (nand_2_out, in_2, in_2);
  nand nand_3 (nand_3_out, nand_1_out, in_2);
  nand nand_4 (nand_4_out, nand_2_out, in_1);
  nand nand_5 (out_3, nand_3_out, nand_4_out);
endmodule

module s_3 (
  input  in_1,
  input  in_2,
  input  in_3,
  input  in_4,
  output out_5
);

  wire and_1_out, and_2_out, and_3_out, and_4_out, not_1_out, not_2_out, not_3_out, not_4_out;

  not not_1 (not_1_out, in_2);
  not not_2 (not_2_out, in_3);
  not not_3 (not_3_out, in_1);
  not not_4 (not_4_out, in_4);
  and and_1 (and_1_out, in_1, in_2, in_3);
  and and_2 (and_2_out, in_1, not_1_out, not_2_out);
  and and_3 (and_3_out, not_3_out, not_1_out, not_4_out);
  and and_4 (and_4_out, not_4_out, not_2_out);
  or or_1 (out_5, and_1_out, and_2_out, and_3_out, and_4_out);
endmodule

module s_4 (
  input  in_1,
  input  in_2,
  input  in_3,
  input  in_4,
  output out_5
);

  wire nand_1_out, nand_2_out, nand_3_out, nand_4_out, nand_5_out, nand_6_out, nand_7_out, nand_8_out,
       nand_9_out, nand_10_out;

  nand nand_1 (nand_1_out, in_1, in_1);
  nand nand_2 (nand_2_out, in_2, in_2);
  nand nand_3 (nand_3_out, in_3, in_3);
  nand nand_4 (nand_4_out, in_4, in_4);
  nand nand_5 (nand_5_out, nand_1_out, nand_3_out, in_2, in_4);
  nand nand_6 (nand_6_out, nand_2_out, nand_3_out, nand_4_out);
  nand nand_7 (nand_7_out, nand_3_out, nand_4_out, in_1);
  nand nand_8 (nand_8_out, in_1, in_2, in_3);
  nand nand_9 (nand_9_out, nand_2_out, in_4, in_3);
  nand nand_10 (nand_10_out, in_4, in_3, in_1);
  nand nand_11 (out_5, nand_5_out, nand_6_out, nand_7_out, nand_8_out, nand_9_out, nand_10_out);
endmodule
