// Logisim project solution-4.circ as structural Verilog: 4 circuits, main circuit main
module main (
  input  in_1,
  input  in_2,
  input  in_3,
  input  in_4,
  input  in_5,
  input  in_6,
  input  in_7,
  input  in_8,
  input  in_9,
  input  in_10,
  input  in_11,
  input  in_12,
  input  in_13,
  input  in_14,
  input  in_15,
  input  in_16,
  input  in_17,
  input  in_18,
  input  in_19,
  input  in_20,
  input  in_21,
  input  in_22,
  input  in_23,
  input  in_24,
  input  in_25,
  input  in_26,
  input  in_27,
  input  in_28,
  input  in_29,
  input  in_30,
  input  in_31,
  input  in_32,
  input  in_33,
  output out_34,
  output out_35,
  output out_36,
  output out_37,
  output out_38,
  output out_39,
  output out_40,
  output out_41,
  output out_42,
  output out_43,
  output out_44,
  output out_45,
  output out_46,
  output out_47,
  output out_48,
  output out_49,
  output out_50,
  output out_51,
  output out_52
);

  wire carry_lookehead_1_out_10, carry_lookehead_1_out_11, carry_lookehead_1_out_12, n4_bit_summary_1_out_15,
       n4_bit_summary_1_out_16, n4_bit_summary_2_out_15, n4_bit_summary_2_out_16, n4_bit_summary_3_out_15,
       n4_bit_summary_3_out_16, n4_bit_summary_4_out_15, n4_bit_summary_4_out_16;

  _4_bit_summary u_4_bit_summary_1 (
    .in_1(in_13), .in_2(in_14), .in_3(in_15), .in_4(in_16), .in_5(in_29), .in_6(in_30), .in_7(in_31),
    .in_8(in_32), .in_9(in_33), .out_13(out_52), .out_12(out_51), .out_10(out_49), .out_11(out_50),
    .out_15(n4_bit_summary_1_out_15), .out_16(n4_bit_summary_1_out_16));  // open: out_14
  carry_lookehead carry_lookehead_1 (
    .in_1(in_33), .in_2(n4_bit_summary_1_out_15), .in_3(n4_bit_summary_1_out_16),
    .in_4(n4_bit_summary_2_out_15), .in_5(n4_bit_summary_2_out_16), .in_6(n4_bit_summary_3_out_15),
    .in_7(n4_bit_summary_3_out_16), .in_8(n4_bit_summary_4_out_15), .out_13(out_34),
    .in_9(n4_bit_summary_4_out_16), .out_12(carry_lookehead_1_out_12), .out_11(carry_lookehead_1_out_11),
    .out_10(carry_lookehead_1_out_10), .out_15(out_36), .out_14(out_35));
  _4_bit_summary u_4_bit_summary_2 (
    .in_1(in_9), .in_2(in_10), .in_3(in_11), .in_4(in_12), .in_5(in_25), .in_6(in_26), .in_7(in_27),
    .in_8(in_28), .in_9(carry_lookehead_1_out_10), .out_13(out_48), .out_12(out_47), .out_10(out_45),
    .out_11(out_46), .out_15(n4_bit_summary_2_out_15), .out_16(n4_bit_summary_2_out_16));  // open: out_14
  _4_bit_summary u_4_bit_summary_3 (
    .in_1(in_5), .in_2(in_6), .in_3(in_7), .in_4(in_8), .in_5(in_21), .in_6(in_22), .in_7(in_23),
    .in_8(in_24), .in_9(carry_lookehead_1_out_11), .out_13(out_44), .out_12(out_43), .out_10(out_41),
    .out_11(out_42), .out_15(n4_bit_summary_3_out_15), .out_16(n4_bit_summary_3_out_16));  // open: out_14
  _4_bit_summary u_4_bit_summary_4 (
    .in_1(in_1), .in_2(in_2), .in_3(in_3), .in_4(in_4), .in_5(in_17), .in_6(in_18), .in_7(in_19),
    .in_8(in_20), .in_9(carry_lookehead_1_out_12), .out_13(out_40), .out_12(out_39), .out_10(out_37),
    .out_11(out_38), .out_15(n4_bit_summary_4_out_15), .out_16(n4_bit_summary_4_out_16));  // open: out_14
endmodule

module summary (
  input  in_1,
  input  in_2,
  input  in_3,
  output out_4,
  output out_5,
  output out_6
);

  xor xor_1 (out_5, in_2, in_3);
  and and_1 (out_6, in_2, in_3);
  xor xor_2 (out_4, in_1, out_5);
endmodule

module _4_bit_summary (
  input  in_1,
  input  in_2,
  input  in_3,
  input  in_4,
  input  in_5,
  input  in_6,
  input  in_7,
  input  in_8,
  input  in_9,
  output out_10,
  output out_11,
  output out_12,
  output out_13,
  output out_14,
  output out_15,
  output out_16
);

  wire carry_lookehead_1_out_10, carry_lookehead_1_out_11, carry_lookehead_1_out_12, summary_1_out_5,
       summary_1_out_6, summary_2_out_5, summary_2_out_6, summary_3_out_5, summary_3_out_6, summary_4_out_5,
       summary_4_out_6;

  summary summary_1 (
    .in_1(in_9), .in_3(in_4), .in_2(in_8), .out_4(out_13), .out_5(summary_1_out_5), .out_6(summary_1_out_6));
  summary summary_2 (
    .in_1(carry_lookehead_1_out_10), .in_3(in_3), .in_2(in_7), .out_4(out_12), .out_5(summary_2_out_5),
    .out_6(summary_2_out_6));
  carry_lookehead carry_lookehead_1 (
    .in_1(in_9), .in_2(summary_1_out_5), .in_3(summary_1_out_6), .in_4(summary_2_out_5),
    .in_5(summary_2_out_6), .in_6(summary_3_out_5), .in_7(summary_3_out_6), .in_8(summary_4_out_5),
    .out_13(out_14), .in_9(summary_4_out_6), .out_12(carry_lookehead_1_out_12),
    .out_11(carry_lookehead_1_out_11), .out_10(carry_lookehead_1_out_10), .out_15(out_16), .out_14(out_15));
  summary summary_3 (
    .in_1(carry_lookehead_1_out_11), .in_3(in_2), .in_2(in_6), .out_4(out_11), .out_5(summary_3_out_5),
    .out_6(summary_3_out_6));
  summary summary_4 (
    .in_1(carry_lookehead_1_out_12), .in_3(in_1), .in_2(in_5), .out_4(out_10), .out_5(summary_4_out_5),
    .out_6(summary_4_out_6));
endmodule

module carry_lookehead (
  input  in_1,
  input  in_2,
  input  in_3,
  input  in_4,
  input  in_5,
  input  in_6,
  input  in_7,
  input  in_8,
  input  in_9,
  output out_10,
  output out_11,
  output out_12,
  output out_13,
  output out_14,
  output out_15
);

  wire and_2_out, and_3_out, and_4_out, and_5_out, and_6_out, and_7_out, and_8_out;

  and and_1 (out_14, in_2, in_4, in_6, in_8);
  and and_2 (and_2_out, in_7, in_8);
  and and_3 (and_3_out, in_5, in_6, in_8);
  or or_1 (out_15, in_9, and_2_out, and_3_out, and_4_out);
  and and_4 (and_4_out, in_3, in_2, in_5, in_8);
  and and_5 (and_5_out, in_1, in_2);
  and and_6 (and_6_out, out_10, in_4);
  and and_7 (and_7_out, out_11, in_6);
  and and_8 (and_8_out, out_12, in_8);
  or or_2 (out_10, and_5_out, in_3);
  or or_3 (out_11, and_6_out, in_5);
  or or_4 (out_12, and_7_out, in_7);
  or or_5 (out_13, and_8_out, in_9);
endmodule
