// Logisim project solution-1.circ as structural Verilog: 1 circuit, main circuit main
module main (
  input  in_1,
  input  in_2,
  output out_3,
  output out_4,
  output out_5,
  output out_6,
  output out_7,
  output out_8,
  output out_9,
  output out_10
);

  wire clock_1_out, clock_2_out, t_ff_1_qn, t_ff_3_qn, t_ff_5_qn;

  Clock clock_1 (.out(clock_1_out));
  Clock clock_2 (.out(clock_2_out));
  T_Flip_Flop t_ff_1 (.clk(clock_1_out), .T(in_1), .Q(out_6), .Qn(t_ff_1_qn));  // open: preset, reset, en
  T_Flip_Flop t_ff_2 (.clk(clock_2_out), .T(in_2), .Q(out_10));  // open: Qn, preset, reset, en
  T_Flip_Flop t_ff_3 (.clk(t_ff_1_qn), .T(in_1), .Q(out_5), .Qn(t_ff_3_qn));  // open: preset, reset, en
  T_Flip_Flop t_ff_4 (.clk(out_10), .T(in_2), .Q(out_9));  // open: Qn, preset, reset, en
  T_Flip_Flop t_ff_5 (.clk(t_ff_3_qn), .T(in_1), .Q(out_4), .Qn(t_ff_5_qn));  // open: preset, reset, en
  T_Flip_Flop t_ff_6 (.clk(out_9), .T(in_2), .Q(out_8));  // open: Qn, preset, reset, en
  T_Flip_Flop t_ff_7 (.clk(t_ff_5_qn), .T(in_1), .Q(out_3));  // open: Qn, preset, reset, en
  T_Flip_Flop t_ff_8 (.clk(out_8), .T(in_2), .Q(out_7));  // open: Qn, preset, reset, en
  Hex_Digit_Display hex_digit_display_1 (.value({out_3, out_4, out_5, out_6}));  // open: dp
  Hex_Digit_Display hex_digit_display_2 (.value({out_7, out_8, out_9, out_10}));  // open: dp
endmodule
