// Logisim project solution-3.circ as structural Verilog: 1 circuit, main circuit main
module main (
  input  in_1,
  input  in_2,
  input  in_3,
  input  in_4,
  input  in_5,
  output out_6,
  output out_7,
  output out_8,
  output out_9
);

  wire clock_1_out, t_ff_1_qn, t_ff_2_qn, t_ff_3_qn, undriven;

  Clock clock_1 (.out(clock_1_out));
  T_Flip_Flop t_ff_1 (.clk(clock_1_out), .T(in_1), .Q(out_9), .Qn(t_ff_1_qn), .reset(undriven));  // open: preset, en
  T_Flip_Flop t_ff_2 (.clk(t_ff_1_qn), .T(in_1), .Q(out_8), .Qn(t_ff_2_qn), .reset(undriven));  // open: preset, en
  T_Flip_Flop t_ff_3 (.clk(t_ff_2_qn), .T(in_1), .Q(out_7), .Qn(t_ff_3_qn), .reset(undriven));  // open: preset, en
  NotExactlyOne xnor_1 (.in0(in_2), .in1(in_3), .in2(in_4), .in3(in_5));  // open: out
  T_Flip_Flop t_ff_4 (.clk(t_ff_3_qn), .T(in_1), .Q(out_6), .reset(undriven));  // open: Qn, preset, en
  Hex_Digit_Display hex_digit_display_1 (.value({out_6, out_7, out_8, out_9}));  // open: dp
endmodule
