// Logisim project solution-4.circ as structural Verilog: 2 circuits, main circuit main
module main (
  input  in_1,
  input  in_2,
  input  in_3,
  input  in_4,
  output out_5,
  output out_6,
  output out_7,
  output out_8
);

  wire clock_1_out, d_ff_1_qn, d_ff_2_qn, d_ff_3_qn, d_ff_4_qn, not_1_out, not_2_out, not_3_out,
       reset_1_out_9;

  Clock clock_1 (.out(clock_1_out));
  D_Flip_Flop d_ff_1 (
    .clk(clock_1_out), .D(d_ff_1_qn), .Q(out_8), .Qn(d_ff_1_qn), .reset(reset_1_out_9));  // open: preset, en
  not not_1 (not_1_out, out_8);
  D_Flip_Flop d_ff_2 (
    .clk(not_1_out), .D(d_ff_2_qn), .Q(out_7), .Qn(d_ff_2_qn), .reset(reset_1_out_9));  // open: preset, en
  reset reset_1 (
    .in_1(in_4), .in_2(out_8), .in_3(in_3), .in_4(out_7), .in_5(in_2), .in_6(out_6), .in_7(in_1),
    .in_8(out_5), .out_9(reset_1_out_9));
  not not_2 (not_2_out, out_7);
  not not_3 (not_3_out, out_6);
  D_Flip_Flop d_ff_3 (
    .clk(not_2_out), .D(d_ff_3_qn), .Q(out_6), .Qn(d_ff_3_qn), .reset(reset_1_out_9));  // open: preset, en
  D_Flip_Flop d_ff_4 (
    .clk(not_3_out), .D(d_ff_4_qn), .Q(out_5), .Qn(d_ff_4_qn), .reset(reset_1_out_9));  // open: preset, en
  Hex_Digit_Display hex_digit_display_1 (.value({out_5, out_6, out_7, out_8}));  // open: dp
endmodule

module reset (
  input  in_1,
  input  in_2,
  input  in_3,
  input  in_4,
  input  in_5,
  input  in_6,
  input  in_7,
  input  in_8,
  output out_9
);

  wire xnor_1_out, xnor_2_out, xnor_3_out, xnor_4_out;

  xnor xnor_1 (xnor_1_out, in_1, in_2);
  xnor xnor_2 (xnor_2_out, in_3, in_4);
  xnor xnor_3 (xnor_3_out, in_5, in_6);
  xnor xnor_4 (xnor_4_out, in_7, in_8);
  and and_1 (out_9, xnor_1_out, xnor_2_out, xnor_3_out, xnor_4_out);
endmodule
