// Logisim project solution-6.circ as structural Verilog: 4 circuits, main circuit main
module main (
  input  in_1,
  input  in_2,
  input  in_3,
  input  in_4,
  input  in_5,
  input  in_6,
  input  in_7,
  input  in_8,
  input  in_9,
  output out_10,
  output out_11,
  output out_12,
  output out_13,
  output out_14,
  output out_15,
  output out_16,
  output out_17
);

  wire and_1_out, clock_1_out, t_ff_1_q, t_ff_1_qn, t_ff_2_q, t_ff_2_qn, t_ff_3_q, t_ff_3_qn, t_ff_4_q;

  Clock clock_1 (.out(clock_1_out));
  T_Flip_Flop t_ff_1 (
    .clk(clock_1_out), .T(in_5), .Q(t_ff_1_q), .Qn(t_ff_1_qn), .reset(and_1_out));  // open: preset, en
  T_Flip_Flop t_ff_2 (.clk(t_ff_1_qn), .T(in_5), .Q(t_ff_2_q), .Qn(t_ff_2_qn), .reset(and_1_out));  // open: preset, en
  T_Flip_Flop t_ff_3 (.clk(t_ff_2_qn), .T(in_5), .Q(t_ff_3_q), .Qn(t_ff_3_qn), .reset(and_1_out));  // open: preset, en
  T_Flip_Flop t_ff_4 (.clk(t_ff_3_qn), .T(in_5), .Q(t_ff_4_q), .reset(and_1_out));  // open: Qn, preset, en
  and and_1 (and_1_out, t_ff_3_q, t_ff_2_q, t_ff_1_q);
  multiplier multiplier_1 (
    .in_9(in_6), .in_10(in_7), .in_11(in_8), .in_12(in_9), .in_1(in_1), .in_2(in_2), .in_3(in_3),
    .in_4(in_4), .in_5(t_ff_4_q), .in_6(t_ff_3_q), .in_7(t_ff_2_q), .in_8(t_ff_1_q), .out_13(out_10),
    .out_14(out_11), .out_15(out_12), .out_16(out_13), .out_17(out_14), .out_18(out_15), .out_19(out_16),
    .out_20(out_17));
  Hex_Digit_Display hex_digit_display_1 (.value({out_10, out_11, out_12, out_13}));  // open: dp
  Hex_Digit_Display hex_digit_display_2 (.value({out_14, out_15, out_16, out_17}));  // open: dp
endmodule

module summary (
  input  in_1,
  input  in_2,
  input  in_3,
  output out_4,
  output out_5
);

  wire and_1_out, and_2_out, xor_1_out;

  xor xor_1 (xor_1_out, in_2, in_3);
  and and_1 (and_1_out, in_2, in_3);
  xor xor_2 (out_4, in_1, xor_1_out);
  and and_2 (and_2_out, in_1, xor_1_out);
  or or_1 (out_5, and_2_out, and_1_out);
endmodule

module _4_bit_summary (
  input  in_1,
  input  in_2,
  input  in_3,
  input  in_4,
  input  in_5,
  input  in_6,
  input  in_7,
  input  in_8,
  input  in_9,
  output out_10,
  output out_11,
  output out_12,
  output out_13,
  output out_14
);

  wire summary_1_out_5, summary_2_out_5, summary_3_out_5;

  summary summary_1 (.in_1(in_4), .in_2(in_8), .in_3(in_9), .out_4(out_14), .out_5(summary_1_out_5));
  summary summary_2 (.in_1(in_3), .in_2(in_7), .in_3(summary_1_out_5), .out_4(out_13), .out_5(summary_2_out_5));
  summary summary_3 (.in_1(in_2), .in_2(in_6), .in_3(summary_2_out_5), .out_4(out_12), .out_5(summary_3_out_5));
  summary summary_4 (.in_1(in_1), .in_2(in_5), .in_3(summary_3_out_5), .out_4(out_11), .out_5(out_10));
endmodule

module multiplier (
  input  in_1,
  input  in_2,
  input  in_3,
  input  in_4,
  input  in_5,
  input  in_6,
  input  in_7,
  input  in_8,
  input  in_9,
  input  in_10,
  input  in_11,
  input  in_12,
  output out_13,
  output out_14,
  output out_15,
  output out_16,
  output out_17,
  output out_18,
  output out_19,
  output out_20
);

  wire and_2_out, and_3_out, and_4_out, and_5_out, and_6_out, and_7_out, and_8_out, and_9_out, and_10_out,
       and_11_out, and_12_out, and_13_out, and_14_out, and_15_out, and_16_out, n4_bit_summary_1_out_10,
       n4_bit_summary_1_out_11, n4_bit_summary_1_out_12, n4_bit_summary_1_out_13, n4_bit_summary_2_out_10,
       n4_bit_summary_2_out_11, n4_bit_summary_2_out_12, n4_bit_summary_2_out_13;

  and and_1 (out_20, in_4, in_8);
  and and_2 (and_2_out, in_1, in_8);
  and and_3 (and_3_out, in_2, in_8);
  and and_4 (and_4_out, in_3, in_8);
  and and_5 (and_5_out, in_1, in_7);
  and and_6 (and_6_out, in_2, in_7);
  and and_7 (and_7_out, in_3, in_7);
  and and_8 (and_8_out, in_4, in_7);
  and and_9 (and_9_out, in_1, in_6);
  and and_10 (and_10_out, in_2, in_6);
  and and_11 (and_11_out, in_3, in_6);
  and and_12 (and_12_out, in_4, in_6);
  and and_13 (and_13_out, in_1, in_5);
  and and_14 (and_14_out, in_2, in_5);
  and and_15 (and_15_out, in_3, in_5);
  and and_16 (and_16_out, in_4, in_5);
  _4_bit_summary u_4_bit_summary_1 (
    .out_10(n4_bit_summary_1_out_10), .in_1(in_9), .in_2(and_2_out), .in_3(and_3_out), .in_4(and_4_out),
    .in_5(and_5_out), .in_6(and_6_out), .in_7(and_7_out), .in_8(and_8_out), .out_11(n4_bit_summary_1_out_11),
    .out_12(n4_bit_summary_1_out_12), .out_13(n4_bit_summary_1_out_13), .out_14(out_19), .in_9(in_10));
  _4_bit_summary u_4_bit_summary_2 (
    .out_10(n4_bit_summary_2_out_10), .in_1(n4_bit_summary_1_out_10), .in_2(n4_bit_summary_1_out_11),
    .in_3(n4_bit_summary_1_out_12), .in_4(n4_bit_summary_1_out_13), .in_5(and_9_out), .in_6(and_10_out),
    .in_7(and_11_out), .in_8(and_12_out), .out_11(n4_bit_summary_2_out_11), .out_12(n4_bit_summary_2_out_12),
    .out_13(n4_bit_summary_2_out_13), .out_14(out_18), .in_9(in_11));
  _4_bit_summary u_4_bit_summary_3 (
    .out_10(out_13), .in_1(n4_bit_summary_2_out_10), .in_2(n4_bit_summary_2_out_11),
    .in_3(n4_bit_summary_2_out_12), .in_4(n4_bit_summary_2_out_13), .in_5(and_13_out), .in_6(and_14_out),
    .in_7(and_15_out), .in_8(and_16_out), .out_11(out_14), .out_12(out_15), .out_13(out_16), .out_14(out_17),
    .in_9(in_12));
endmodule
