// Logisim project solution-3.circ as structural Verilog: 2 circuits, main circuit main
module main (
  input  in_1,
  input  in_2,
  input  in_3,
  input  in_4,
  input  in_5,
  output out_6,
  output out_7,
  output out_8,
  output out_9
);

  wire clock_1_out, reset_1_out_9, t_ff_1_qn, t_ff_2_qn, t_ff_3_qn;

  Clock clock_1 (.out(clock_1_out));
  T_Flip_Flop t_ff_1 (
    .clk(clock_1_out), .T(in_1), .Q(out_9), .Qn(t_ff_1_qn), .reset(reset_1_out_9));  // open: preset, en
  T_Flip_Flop t_ff_2 (.clk(t_ff_1_qn), .T(in_1), .Q(out_8), .Qn(t_ff_2_qn), .reset(reset_1_out_9));  // open: preset, en
  reset reset_1 (
    .in_1(in_5), .in_2(out_9), .in_3(in_4), .in_4(out_8), .in_5(in_3), .in_6(out_7), .in_7(in_2),
    .in_8(out_6), .out_9(reset_1_out_9));
  T_Flip_Flop t_ff_3 (.clk(t_ff_2_qn), .T(in_1), .Q(out_7), .Qn(t_ff_3_qn), .reset(reset_1_out_9));  // open: preset, en
  T_Flip_Flop t_ff_4 (.clk(t_ff_3_qn), .T(in_1), .Q(out_6), .reset(reset_1_out_9));  // open: Qn, preset, en
  Hex_Digit_Display hex_digit_display_1 (.value({out_6, out_7, out_8, out_9}));  // open: dp
endmodule

module reset (
  input  in_1,
  input  in_2,
  input  in_3,
  input  in_4,
  input  in_5,
  input  in_6,
  input  in_7,
  input  in_8,
  output out_9
);

  wire xnor_1_out, xnor_2_out, xnor_3_out, xnor_4_out;

  xnor xnor_1 (xnor_1_out, in_1, in_2);
  xnor xnor_2 (xnor_2_out, in_3, in_4);
  xnor xnor_3 (xnor_3_out, in_5, in_6);
  xnor xnor_4 (xnor_4_out, in_7, in_8);
  and and_1 (out_9, xnor_1_out, xnor_2_out, xnor_3_out, xnor_4_out);
endmodule
