// Logisim project solution-2.circ as structural Verilog: 2 circuits, main circuit main
module main (
  input  in_1,
  input  in_2,
  input  in_3,
  input  in_4,
  input  in_5,
  input  in_6,
  input  in_7,
  input  in_8,
  input  in_9,
  output out_10,
  output out_11,
  output out_12,
  output out_13,
  output out_14
);

  wire summary_1_out_5, summary_2_out_5, summary_3_out_5;

  summary summary_1 (.in_1(in_9), .in_2(in_4), .in_3(in_8), .out_4(out_14), .out_5(summary_1_out_5));
  summary summary_2 (.in_1(summary_1_out_5), .in_2(in_3), .in_3(in_7), .out_4(out_13), .out_5(summary_2_out_5));
  summary summary_3 (.in_1(summary_2_out_5), .in_2(in_2), .in_3(in_6), .out_4(out_12), .out_5(summary_3_out_5));
  summary summary_4 (.in_1(summary_3_out_5), .in_2(in_1), .in_3(in_5), .out_4(out_11), .out_5(out_10));
endmodule

module summary (
  input  in_1,
  input  in_2,
  input  in_3,
  output out_4,
  output out_5
);

  wire and_1_out, and_2_out, xor_1_out;

  xor xor_1 (xor_1_out, in_2, in_3);
  and and_1 (and_1_out, in_2, in_3);
  xor xor_2 (out_4, in_1, xor_1_out);
  and and_2 (and_2_out, in_1, xor_1_out);
  or or_1 (out_5, and_2_out, and_1_out);
endmodule
